// Digital circuit QT Sandbox.dig as structural Verilog
module QT_Sandbox (
  input  clk
);

  wire Power_out, qtc_1_p6, qtc_1_p7, qtc_1_p8;

  Button Power (.out(Power_out));
  // QTC qtc_1: pin names not known; wires that end beside it: Power_out, clk, 1'b0, {8{1'b0}}, 1'b0, qtc_1_p6, qtc_1_p7, qtc_1_p8
  LED led_1 (.in(qtc_1_p6));
  Terminal terminal_1 (.D(qtc_1_p7), .C(clk), .en(qtc_1_p8));

  // Notes on the sheet:
  //   clk: Hz: 32
  //   Set up for: Hello World
endmodule
